// Logisim project sap-1-computer.circ as structural Verilog: 18 circuits, main circuit control Unit
module main (
  input  CLR,
  output [3:0] Low,
  output [3:0] High
);

  wire CLK_out, control_unit_1_cp, control_unit_1_ea, control_unit_1_ep, control_unit_1_eu,
       control_unit_1_hlt, control_unit_1_nce, control_unit_1_nel, control_unit_1_nla, control_unit_1_nlb,
       control_unit_1_nll, control_unit_1_nlm, control_unit_1_nlo, control_unit_1_su,
       controlled_buffer_1_out, not_1_out, not_2_out, not_3_out, not_4_out, not_5_out;
  wire [3:0] ir_1_to_controller, mar_1_to_ram, output_register_1_output_to_binary_display,
       output_register_1_output_to_binary_display_2;
  wire [7:0] accmolator_1_output_to_adder_substractor, b_register_1_output_to_adder_subtractor;

  Hex_Digit_Display hex_digit_display_1 (.value(High));  // open: dp
  Program_Counter program_counter_1 (
    .CP(control_unit_1_cp), .EP(control_unit_1_ep), .nCLK(controlled_buffer_1_out), .CLR(CLR), .Enable(1'b1),
    .pc_output(Low));
  Hex_Digit_Display hex_digit_display_2 (.value(Low));  // open: dp
  Hex_Digit_Display hex_digit_display_3 (.value(Low));  // open: dp
  MAR mar_1 (
    .ENABLE(1'b1), .nLm(control_unit_1_nlm), .CLR(CLR), .CLK(controlled_buffer_1_out), .FROM_BUS(Low),
    .TO_RAM(mar_1_to_ram));
  not not_1 (not_1_out, control_unit_1_nce);
  IR ir_1 (
    .To_Controller(ir_1_to_controller), .ENABLE(1'b1), .CLK(controlled_buffer_1_out), .CLR(CLR),
    .From_Bus({High, Low}), .nLi(control_unit_1_nll), .nEi(control_unit_1_nel), .To_Bus(Low));
  control_Unit control_unit_1 (
    .CLK(controlled_buffer_1_out), .Ep(control_unit_1_ep), .Cp(control_unit_1_cp),
    .l7(ir_1_to_controller[3]), .l6(ir_1_to_controller[2]), .l5(ir_1_to_controller[1]),
    .l4(ir_1_to_controller[0]), .HLT(control_unit_1_hlt), .nLm(control_unit_1_nlm), .nCE(control_unit_1_nce),
    .nEl(control_unit_1_nel), .nLa(control_unit_1_nla), .Ea(control_unit_1_ea), .Su(control_unit_1_su),
    .Eu(control_unit_1_eu), .nLb(control_unit_1_nlb), .nLo(control_unit_1_nlo), .nLl(control_unit_1_nll));
  Hex_Digit_Display hex_digit_display_4 (.value(Low));  // open: dp
  RAM #(.addrWidth(4)) ram_1 (.addr(mar_1_to_ram), .data({High, Low}), .ld(not_1_out));  // open: sel, clk, clr
  Hex_Digit_Display hex_digit_display_5 (.value(High));  // open: dp
  Hex_Digit_Display hex_digit_display_6 (.value(Low));  // open: dp
  accmolator accmolator_1 (
    .Input_From_Bus({High, Low}), .Output_To_Adder_Substractor(accmolator_1_output_to_adder_substractor),
    .Ea(control_unit_1_ea), .La(not_2_out), .CLK(controlled_buffer_1_out), .Clr(CLR), .Enable(1'b1),
    .Output_To_Bus({High, Low}));
  not not_2 (not_2_out, control_unit_1_nla);
  not not_3 (not_3_out, control_unit_1_nlb);
  Output_Register output_register_1 (
    .Input_From_Bus({High, Low}), .Lo(not_4_out), .CLK(controlled_buffer_1_out), .CLR(CLR), .Enable(1'b1),
    .Output_To_Binary_Display({output_register_1_output_to_binary_display_2, output_register_1_output_to_binary_display}));
  not not_4 (not_4_out, control_unit_1_nlo);
  ALU alu_1 (
    .From_B_Register(b_register_1_output_to_adder_subtractor), .Su(control_unit_1_su),
    .Eu(control_unit_1_eu), .Output_To_Bus({High, Low}),
    .From_Accumulator(accmolator_1_output_to_adder_substractor));
  B_Register b_register_1 (
    .Input_From_Bus({High, Low}), .Lb(not_3_out), .CLK(controlled_buffer_1_out), .CLR(CLR), .Enable(1'b1),
    .Output_To_Adder_Subtractor(b_register_1_output_to_adder_subtractor));
  LED led_1 (.in(output_register_1_output_to_binary_display_2[2]));
  LED led_2 (.in(output_register_1_output_to_binary_display_2[3]));
  Clock CLK (.out(CLK_out));
  not not_5 (not_5_out, control_unit_1_hlt);
  assign controlled_buffer_1_out = not_5_out ? CLK_out : 1'bz;  // Controlled_Buffer controlled_buffer_1
  LED led_3 (.in(output_register_1_output_to_binary_display_2[1]));
  LED led_4 (.in(output_register_1_output_to_binary_display_2[0]));
  Hex_Digit_Display hex_digit_display_7 (.value(accmolator_1_output_to_adder_substractor[7:4]));  // open: dp
  LED led_5 (.in(output_register_1_output_to_binary_display[3]));
  LED led_6 (.in(output_register_1_output_to_binary_display[2]));
  Hex_Digit_Display hex_digit_display_8 (.value(accmolator_1_output_to_adder_substractor[3:0]));  // open: dp
  LED led_7 (.in(output_register_1_output_to_binary_display[0]));
  LED led_8 (.in(output_register_1_output_to_binary_display[1]));
  Hex_Digit_Display hex_digit_display_9 (.value(output_register_1_output_to_binary_display_2));  // open: dp
  Hex_Digit_Display hex_digit_display_10 (.value(output_register_1_output_to_binary_display));  // open: dp

  // Notes on the sheet:
  //   Cp
  //   Ep
  //   Hex Display
  //   ~Lm
  //   To Bus
  //   To RAM
  //   From Bus
  //   ~CE
  //   Cp
  //   Ep
  //   ~Ei
  //   ~Li
  //   To Controller
  //   Controller
  //   To Bus
  //   To Bus
  //   From Bus
  //    SAP-1  computer 
  //   From Bus
  //   ~La
  //   To Bus
  //   ~Lo
  //   To Bus
  //   Ea
  //   ~Lb
  //   Eu
  //   Hex Display
  //   Su
  //   CLR
  //   clk
endmodule

module control_Unit (
  input  CLK,
  input  l4,
  input  l5,
  input  l6,
  input  l7,
  output Ep,
  output Cp,
  output HLT,
  output nLm,
  output nCE,
  output nEl,
  output nLa,
  output Ea,
  output Su,
  output Eu,
  output nLb,
  output nLo,
  output nLl
);

  wire instruction_decoder_1_add, instruction_decoder_1_load, instruction_decoder_1_out,
       instruction_decoder_1_sub, not_1_out, ring_counter_1_t3, ring_counter_1_t4, ring_counter_1_t5,
       ring_counter_1_t6, sub_con1_1_out_7, sub_con1_1_out_8, sub_con1_1_out_9, sub_con1_1_out_10,
       sub_con2_1_out_7, sub_con2_1_out_8, sub_con2_1_out_9, sub_con2_1_out_10, sub_con3_1_out_8,
       sub_con3_1_out_9, sub_con3_1_out_10, sub_con3_1_out_11, sub_con3_2_out_10, sub_con3_2_out_11,
       sub_con4_1_out_6, sub_con4_1_out_7, sub_con4_1_out_8;

  Instruction_Decoder instruction_decoder_1 (
    .in_1(l7), .in_2(l6), .in_3(l5), .in_4(l4), .Load(instruction_decoder_1_load),
    .Add(instruction_decoder_1_add), .Sub(instruction_decoder_1_sub), .Out(instruction_decoder_1_out),
    .Halt(HLT));
  Sub_con1 sub_con1_1 (
    ._1(instruction_decoder_1_load), ._4(instruction_decoder_1_add), ._9(instruction_decoder_1_sub),
    ._10(ring_counter_1_t4), ._12(instruction_decoder_1_load), ._13(ring_counter_1_t5),
    .out_7(sub_con1_1_out_7), .out_8(sub_con1_1_out_8), .out_9(sub_con1_1_out_9), .out_10(sub_con1_1_out_10));
  nor nor_1 (nLm, Ep, sub_con1_1_out_7, sub_con1_1_out_8, sub_con1_1_out_9);
  RING_COUNTER ring_counter_1 (
    .CLK(not_1_out), .T1(Ep), .T2(Cp), .T3(ring_counter_1_t3), .T4(ring_counter_1_t4),
    .T5(ring_counter_1_t5), .T6(ring_counter_1_t6));
  not not_1 (not_1_out, CLK);
  Sub_con2 sub_con2_1 (
    ._1(instruction_decoder_1_add), ._4(instruction_decoder_1_sub), ._5(ring_counter_1_t5),
    ._9(instruction_decoder_1_load), ._12(instruction_decoder_1_add), ._13(ring_counter_1_t4),
    .out_7(sub_con2_1_out_7), .out_8(sub_con2_1_out_8), .out_9(sub_con2_1_out_9), .out_10(sub_con2_1_out_10));
  nor nor_2 (nCE, ring_counter_1_t3, sub_con1_1_out_10, sub_con2_1_out_7, sub_con2_1_out_8);
  Sub_con3 sub_con3_1 (
    ._1(instruction_decoder_1_sub), ._2(ring_counter_1_t4), ._4(instruction_decoder_1_load),
    ._5(ring_counter_1_t5), ._9(instruction_decoder_1_add), ._12(instruction_decoder_1_sub),
    ._13(ring_counter_1_t6), .out_8(sub_con3_1_out_8), .out_9(sub_con3_1_out_9), .out_10(sub_con3_1_out_10),
    .out_11(sub_con3_1_out_11));
  nor nor_3 (nEl, sub_con2_1_out_9, sub_con2_1_out_10, sub_con3_1_out_8);
  nor nor_4 (nLa, sub_con3_1_out_9, sub_con3_1_out_10, sub_con3_1_out_11);
  Sub_con3 sub_con3_2 (
    ._1(instruction_decoder_1_out), ._2(ring_counter_1_t4), ._4(instruction_decoder_1_sub),
    ._5(ring_counter_1_t6), ._9(instruction_decoder_1_add), ._12(instruction_decoder_1_sub),
    ._13(ring_counter_1_t6), .out_8(Ea), .out_9(Su), .out_10(sub_con3_2_out_10), .out_11(sub_con3_2_out_11));
  or or_1 (Eu, sub_con3_2_out_10, sub_con3_2_out_11);
  Sub_con4 sub_con4_1 (
    ._1(instruction_decoder_1_add), ._4(instruction_decoder_1_sub), ._5(ring_counter_1_t5),
    ._9(instruction_decoder_1_out), ._10(ring_counter_1_t4), .out_6(sub_con4_1_out_6),
    .out_7(sub_con4_1_out_7), .out_8(sub_con4_1_out_8));
  nor nor_5 (nLb, sub_con4_1_out_6, sub_con4_1_out_7);
  not not_2 (nLo, sub_con4_1_out_8);
  not not_3 (nLl, ring_counter_1_t3);

  // Notes on the sheet:
  //   control unit 
  //   1607028-1607041
endmodule

module Sub_con2 (
  input  _1,
  input  _4,
  input  _5,
  input  _9,
  input  _12,
  input  _13,
  output out_7,
  output out_8,
  output out_9,
  output out_10
);

  and and_1 (out_7, _1, _5);
  and and_2 (out_8, _4, _5);
  and and_3 (out_9, _9, _13);
  and and_4 (out_10, _12, _13);

  // Notes on the sheet:
  //   Fig - Sub-Module2
endmodule

module Sub_con1 (
  input  _1,
  input  _4,
  input  _9,
  input  _10,
  input  _12,
  input  _13,
  output out_7,
  output out_8,
  output out_9,
  output out_10
);

  and and_1 (out_7, _1, _10);
  and and_2 (out_9, _9, _10);
  and and_3 (out_8, _4, _10);
  and and_4 (out_10, _12, _13);

  // Notes on the sheet:
  //   1607028
  //   Fig - Sub-Module1
endmodule

module Sub_con3 (
  input  _4,
  input  _5,
  input  _12,
  input  _13,
  input  _1,
  input  _2,
  input  _9,
  output out_8,
  output out_9,
  output out_10,
  output out_11
);

  and and_1 (out_8, _1, _2);
  and and_2 (out_9, _4, _5);
  and and_3 (out_10, _9, _13);
  and and_4 (out_11, _12, _13);

  // Notes on the sheet:
  //   Fig - Sub-Module3
endmodule

module Sub_con4 (
  input  _1,
  input  _4,
  input  _5,
  input  _9,
  input  _10,
  output out_6,
  output out_7,
  output out_8
);

  and and_1 (out_6, _1, _5);
  and and_2 (out_7, _4, _5);
  and and_3 (out_8, _9, _10);
endmodule

// ID
module Instruction_Decoder (
  input  in_1,
  input  in_2,
  input  in_3,
  input  in_4,
  output Load,
  output Add,
  output Sub,
  output Out,
  output Halt
);

  wire and_1_out, and_2_out, and_3_out, and_4_out, and_5_out, not_1_out, not_2_out, not_3_out, not_4_out;

  not not_1 (not_1_out, in_1);
  not not_2 (not_2_out, in_2);
  not not_3 (not_3_out, in_3);
  not not_4 (not_4_out, in_4);
  and and_1 (and_1_out, not_1_out, not_2_out, not_4_out, not_3_out);
  and and_2 (and_2_out, not_1_out, not_2_out, in_4, not_3_out);
  and and_3 (and_3_out, not_1_out, not_2_out, not_4_out, in_3);
  and and_4 (and_4_out, in_1, in_2, not_4_out, in_3);
  and and_5 (and_5_out, in_1, in_2, in_4, in_3);
  buf buffer_1 (Add, and_2_out);
  buf buffer_2 (Sub, and_3_out);
  buf buffer_3 (Out, and_4_out);
  buf buffer_4 (Halt, and_5_out);
  buf buffer_5 (Load, and_1_out);

  // Notes on the sheet:
  //    Instruction Decoder
  //   1607028
endmodule

// Counter
module Program_Counter (
  input  CP,
  input  EP,
  input  nCLK,
  input  CLR,
  input  Enable,
  output [3:0] pc_output
);

  wire ha_1_sum, ha_2_carry, ha_2_sum, ha_3_carry, ha_3_sum, ha_4_carry, ha_4_sum, not_1_out;
  wire [3:0] d_ff_4_q;

  not not_1 (not_1_out, nCLK);
  LED led_1 (.in(Enable));
  HA ha_1 (.A(d_ff_4_q[3]), .B(ha_2_carry), .Sum(ha_1_sum));  // open: Carry
  D_Flip_Flop d_ff_1 (.clk(not_1_out), .D(ha_1_sum), .Q(d_ff_4_q[3]), .en(Enable), .reset(CLR));  // open: Qn, preset
  HA ha_2 (.A(d_ff_4_q[2]), .B(ha_3_carry), .Sum(ha_2_sum), .Carry(ha_2_carry));
  D_Flip_Flop d_ff_2 (.clk(not_1_out), .D(ha_2_sum), .Q(d_ff_4_q[2]), .en(Enable), .reset(CLR));  // open: Qn, preset
  HA ha_3 (.A(d_ff_4_q[1]), .B(ha_4_carry), .Sum(ha_3_sum), .Carry(ha_3_carry));
  D_Flip_Flop d_ff_3 (.clk(not_1_out), .D(ha_3_sum), .Q(d_ff_4_q[1]), .en(Enable), .reset(CLR));  // open: Qn, preset
  HA ha_4 (.A(d_ff_4_q[0]), .B(CP), .Sum(ha_4_sum), .Carry(ha_4_carry));
  D_Flip_Flop d_ff_4 (.clk(not_1_out), .D(ha_4_sum), .Q(d_ff_4_q[0]), .en(Enable), .reset(CLR));  // open: Qn, preset
  assign pc_output = EP ? d_ff_4_q : 4'bz;  // Controlled_Buffer controlled_buffer_1

  // Notes on the sheet:
  //   Program Counter
endmodule

module HA (
  input  A,
  input  B,
  output Sum,
  output Carry
);

  xor xor_1 (Sum, A, B);
  and and_1 (Carry, B, A);

  // Notes on the sheet:
  //   Fig: Half Adder
endmodule

module MAR (
  input  ENABLE,
  input  nLm,
  input  CLR,
  input  CLK,
  input  [3:0] FROM_BUS,
  output [3:0] TO_RAM
);

  wire not_1_out;
  wire [3:0] controlled_buffer_1_out;

  not not_1 (not_1_out, nLm);
  assign controlled_buffer_1_out = not_1_out ? FROM_BUS : 4'bz;  // Controlled_Buffer controlled_buffer_1
  Tri_state tri_state_1 (
    .x3(controlled_buffer_1_out[0]), .x2(controlled_buffer_1_out[1]), .x1(controlled_buffer_1_out[2]),
    .x0(controlled_buffer_1_out[3]), .CLK(CLK), .LOAD(not_1_out), .CLR(CLR), .ENABLE(ENABLE), .Y3(TO_RAM[0]),
    .Y2(TO_RAM[1]), .Y1(TO_RAM[2]), .Y0(TO_RAM[3]));

  // Notes on the sheet:
  //    Memory Address Register
endmodule

// Register
module Tri_state (
  input  x3,
  input  x2,
  input  x1,
  input  x0,
  input  LOAD,
  input  CLK,
  input  CLR,
  input  ENABLE,
  output Y3,
  output Y2,
  output Y1,
  output Y0
);

  wire and_1_out, and_2_out, and_3_out, and_4_out, and_5_out, and_6_out, and_7_out, and_8_out, d_ff_1_q,
       d_ff_2_q, d_ff_3_q, d_ff_4_q, not_1_out, or_1_out, or_2_out, or_3_out, or_4_out;

  and and_1 (and_1_out, x3, LOAD);
  and and_2 (and_2_out, d_ff_1_q, not_1_out);
  or or_1 (or_1_out, and_2_out, and_1_out);
  assign Y3 = ENABLE ? d_ff_1_q : 1'bz;  // Controlled_Buffer controlled_buffer_1
  D_Flip_Flop d_ff_1 (.clk(CLK), .D(or_1_out), .Q(d_ff_1_q), .reset(CLR));  // open: Qn, preset, en
  and and_3 (and_3_out, d_ff_2_q, not_1_out);
  and and_4 (and_4_out, x2, LOAD);
  or or_2 (or_2_out, and_3_out, and_4_out);
  assign Y2 = ENABLE ? d_ff_2_q : 1'bz;  // Controlled_Buffer controlled_buffer_2
  D_Flip_Flop d_ff_2 (.clk(CLK), .D(or_2_out), .Q(d_ff_2_q), .reset(CLR));  // open: Qn, preset, en
  and and_5 (and_5_out, x1, LOAD);
  and and_6 (and_6_out, d_ff_3_q, not_1_out);
  or or_3 (or_3_out, and_6_out, and_5_out);
  assign Y1 = ENABLE ? d_ff_3_q : 1'bz;  // Controlled_Buffer controlled_buffer_3
  and and_7 (and_7_out, d_ff_4_q, not_1_out);
  D_Flip_Flop d_ff_3 (.clk(CLK), .D(or_3_out), .Q(d_ff_3_q), .reset(CLR));  // open: Qn, preset, en
  and and_8 (and_8_out, x0, LOAD);
  or or_4 (or_4_out, and_7_out, and_8_out);
  assign Y0 = ENABLE ? d_ff_4_q : 1'bz;  // Controlled_Buffer controlled_buffer_4
  not not_1 (not_1_out, LOAD);
  D_Flip_Flop d_ff_4 (.clk(CLK), .D(or_4_out), .Q(d_ff_4_q), .reset(CLR));  // open: Qn, preset, en

  // Notes on the sheet:
  //   rigister
  //   Fig: Tri-State Register
endmodule

module IR (
  input  nEi,
  input  ENABLE,
  input  CLK,
  input  CLR,
  input  nLi,
  input  [7:0] From_Bus,
  output [3:0] To_Bus,
  output [3:0] To_Controller
);

  wire not_1_out, not_2_out;
  wire [3:0] tri_state_2_y3;

  not not_1 (not_1_out, nLi);
  Tri_state tri_state_1 (
    .x3(From_Bus[4]), .x2(From_Bus[5]), .x1(From_Bus[6]), .x0(From_Bus[7]), .CLK(CLK), .LOAD(not_1_out),
    .CLR(CLR), .ENABLE(ENABLE), .Y3(To_Controller[0]), .Y2(To_Controller[1]), .Y1(To_Controller[2]),
    .Y0(To_Controller[3]));
  Tri_state tri_state_2 (
    .x3(From_Bus[0]), .x2(From_Bus[1]), .x1(From_Bus[2]), .x0(From_Bus[3]), .CLK(CLK), .LOAD(not_1_out),
    .CLR(CLR), .ENABLE(ENABLE), .Y3(tri_state_2_y3[0]), .Y2(tri_state_2_y3[1]), .Y1(tri_state_2_y3[2]),
    .Y0(tri_state_2_y3[3]));
  assign To_Bus = not_2_out ? tri_state_2_y3 : 4'bz;  // Controlled_Buffer controlled_buffer_1
  not not_2 (not_2_out, nEi);

  // Notes on the sheet:
  //   Instruction Register
  //   160702
endmodule

// A
module accmolator (
  input  [7:0] Input_From_Bus,
  input  La,
  input  CLK,
  input  Clr,
  input  Enable,
  input  Ea,
  output [7:0] Output_To_Adder_Substractor,
  output [7:0] Output_To_Bus
);

  wire and_1_out, and_2_out, and_3_out, and_4_out, and_5_out, and_6_out, and_7_out, and_8_out, and_9_out,
       and_10_out, and_11_out, and_12_out, and_13_out, and_14_out, and_15_out, and_16_out, not_1_out,
       or_1_out, or_2_out, or_3_out, or_4_out, or_5_out, or_6_out, or_7_out, or_8_out;

  and and_1 (and_1_out, Output_To_Adder_Substractor[7], not_1_out);
  and and_2 (and_2_out, Input_From_Bus[7], La);
  or or_1 (or_1_out, and_1_out, and_2_out);
  D_Flip_Flop d_ff_1 (
    .clk(CLK), .D(or_1_out), .Q(Output_To_Adder_Substractor[7]), .en(Enable), .reset(Clr));  // open: Qn, preset
  and and_3 (and_3_out, Output_To_Adder_Substractor[6], not_1_out);
  and and_4 (and_4_out, Input_From_Bus[6], La);
  or or_2 (or_2_out, and_3_out, and_4_out);
  and and_5 (and_5_out, Output_To_Adder_Substractor[5], not_1_out);
  or or_3 (or_3_out, and_5_out, and_6_out);
  D_Flip_Flop d_ff_2 (
    .clk(CLK), .D(or_2_out), .Q(Output_To_Adder_Substractor[6]), .en(Enable), .reset(Clr));  // open: Qn, preset
  and and_6 (and_6_out, Input_From_Bus[5], La);
  D_Flip_Flop d_ff_3 (
    .clk(CLK), .D(or_3_out), .Q(Output_To_Adder_Substractor[5]), .en(Enable), .reset(Clr));  // open: Qn, preset
  and and_7 (and_7_out, Input_From_Bus[4], La);
  and and_8 (and_8_out, Output_To_Adder_Substractor[4], not_1_out);
  or or_4 (or_4_out, and_8_out, and_7_out);
  D_Flip_Flop d_ff_4 (
    .clk(CLK), .D(or_4_out), .Q(Output_To_Adder_Substractor[4]), .en(Enable), .reset(Clr));  // open: Qn, preset
  and and_9 (and_9_out, Input_From_Bus[3], La);
  and and_10 (and_10_out, Output_To_Adder_Substractor[3], not_1_out);
  or or_5 (or_5_out, and_10_out, and_9_out);
  and and_11 (and_11_out, Output_To_Adder_Substractor[2], not_1_out);
  D_Flip_Flop d_ff_5 (
    .clk(CLK), .D(or_5_out), .Q(Output_To_Adder_Substractor[3]), .en(Enable), .reset(Clr));  // open: Qn, preset
  assign Output_To_Bus = Ea ? Output_To_Adder_Substractor : 8'bz;  // Controlled_Buffer controlled_buffer_1
  and and_12 (and_12_out, Input_From_Bus[2], La);
  or or_6 (or_6_out, and_11_out, and_12_out);
  D_Flip_Flop d_ff_6 (
    .clk(CLK), .D(or_6_out), .Q(Output_To_Adder_Substractor[2]), .en(Enable), .reset(Clr));  // open: Qn, preset
  and and_13 (and_13_out, Input_From_Bus[1], La);
  and and_14 (and_14_out, Output_To_Adder_Substractor[1], not_1_out);
  or or_7 (or_7_out, and_14_out, and_13_out);
  D_Flip_Flop d_ff_7 (
    .clk(CLK), .D(or_7_out), .Q(Output_To_Adder_Substractor[1]), .en(Enable), .reset(Clr));  // open: Qn, preset
  not not_1 (not_1_out, La);
  and and_15 (and_15_out, Input_From_Bus[0], La);
  and and_16 (and_16_out, Output_To_Adder_Substractor[0], not_1_out);
  or or_8 (or_8_out, and_16_out, and_15_out);
  D_Flip_Flop d_ff_8 (
    .clk(CLK), .D(or_8_out), .Q(Output_To_Adder_Substractor[0]), .en(Enable), .reset(Clr));  // open: Qn, preset

  // Notes on the sheet:
  //   Accumulator
endmodule

// B
module B_Register (
  input  [7:0] Input_From_Bus,
  input  Lb,
  input  CLK,
  input  CLR,
  input  Enable,
  output [7:0] Output_To_Adder_Subtractor
);

  wire and_1_out, and_2_out, and_3_out, and_4_out, and_5_out, and_6_out, and_7_out, and_8_out, and_9_out,
       and_10_out, and_11_out, and_12_out, and_13_out, and_14_out, and_15_out, and_16_out, not_1_out,
       or_1_out, or_2_out, or_3_out, or_4_out, or_5_out, or_6_out, or_7_out, or_8_out;

  and and_1 (and_1_out, Output_To_Adder_Subtractor[7], not_1_out);
  or or_1 (or_1_out, and_1_out, and_2_out);
  and and_2 (and_2_out, Input_From_Bus[7], Lb);
  D_Flip_Flop d_ff_1 (
    .clk(CLK), .D(or_1_out), .Q(Output_To_Adder_Subtractor[7]), .en(Enable), .reset(CLR));  // open: Qn, preset
  and and_3 (and_3_out, Input_From_Bus[6], Lb);
  and and_4 (and_4_out, Output_To_Adder_Subtractor[6], not_1_out);
  or or_2 (or_2_out, and_4_out, and_3_out);
  D_Flip_Flop d_ff_2 (
    .clk(CLK), .D(or_2_out), .Q(Output_To_Adder_Subtractor[6]), .en(Enable), .reset(CLR));  // open: Qn, preset
  and and_5 (and_5_out, Output_To_Adder_Subtractor[5], not_1_out);
  and and_6 (and_6_out, Input_From_Bus[5], Lb);
  or or_3 (or_3_out, and_5_out, and_6_out);
  and and_7 (and_7_out, Output_To_Adder_Subtractor[4], not_1_out);
  D_Flip_Flop d_ff_3 (
    .clk(CLK), .D(or_3_out), .Q(Output_To_Adder_Subtractor[5]), .en(Enable), .reset(CLR));  // open: Qn, preset
  and and_8 (and_8_out, Input_From_Bus[4], Lb);
  or or_4 (or_4_out, and_7_out, and_8_out);
  D_Flip_Flop d_ff_4 (
    .clk(CLK), .D(or_4_out), .Q(Output_To_Adder_Subtractor[4]), .en(Enable), .reset(CLR));  // open: Qn, preset
  and and_9 (and_9_out, Input_From_Bus[3], Lb);
  and and_10 (and_10_out, Output_To_Adder_Subtractor[3], not_1_out);
  or or_5 (or_5_out, and_10_out, and_9_out);
  D_Flip_Flop d_ff_5 (
    .clk(CLK), .D(or_5_out), .Q(Output_To_Adder_Subtractor[3]), .en(Enable), .reset(CLR));  // open: Qn, preset
  and and_11 (and_11_out, Input_From_Bus[2], Lb);
  and and_12 (and_12_out, Output_To_Adder_Subtractor[2], not_1_out);
  or or_6 (or_6_out, and_12_out, and_11_out);
  and and_13 (and_13_out, Output_To_Adder_Subtractor[1], not_1_out);
  D_Flip_Flop d_ff_6 (
    .clk(CLK), .D(or_6_out), .Q(Output_To_Adder_Subtractor[2]), .en(Enable), .reset(CLR));  // open: Qn, preset
  and and_14 (and_14_out, Input_From_Bus[1], Lb);
  or or_7 (or_7_out, and_13_out, and_14_out);
  D_Flip_Flop d_ff_7 (
    .clk(CLK), .D(or_7_out), .Q(Output_To_Adder_Subtractor[1]), .en(Enable), .reset(CLR));  // open: Qn, preset
  and and_15 (and_15_out, Output_To_Adder_Subtractor[0], not_1_out);
  or or_8 (or_8_out, and_15_out, and_16_out);
  not not_1 (not_1_out, Lb);
  and and_16 (and_16_out, Input_From_Bus[0], Lb);
  D_Flip_Flop d_ff_8 (
    .clk(CLK), .D(or_8_out), .Q(Output_To_Adder_Subtractor[0]), .en(Enable), .reset(CLR));  // open: Qn, preset

  // Notes on the sheet:
  //   1607041
  //   Fig- B-Register
endmodule

module Full_Adder (
  input  A,
  input  B,
  input  Cin,
  output S,
  output Cout
);

  wire and_1_out, and_2_out, xor_1_out;

  xor xor_1 (xor_1_out, A, B);
  and and_1 (and_1_out, A, B);
  xor xor_2 (S, xor_1_out, Cin);
  and and_2 (and_2_out, xor_1_out, Cin);
  or or_1 (Cout, and_2_out, and_1_out);

  // Notes on the sheet:
  //   Full Adder
endmodule

// Add-Sub
module ALU (
  input  [7:0] From_B_Register,
  input  Su,
  input  Eu,
  input  [7:0] From_Accumulator,
  output [7:0] Output_To_Bus
);

  wire full_adder_1_s, full_adder_2_cout, full_adder_2_s, full_adder_3_cout, full_adder_3_s,
       full_adder_4_cout, full_adder_4_s, full_adder_5_cout, full_adder_5_s, full_adder_6_cout,
       full_adder_6_s, full_adder_7_cout, full_adder_7_s, full_adder_8_cout, full_adder_8_s, xor_1_out,
       xor_2_out, xor_3_out, xor_4_out, xor_5_out, xor_6_out, xor_7_out, xor_8_out;

  Full_Adder full_adder_1 (
    .A(From_Accumulator[7]), .B(xor_1_out), .Cin(full_adder_2_cout), .S(full_adder_1_s));  // open: Cout
  assign Output_To_Bus[7] = Eu ? full_adder_1_s : 1'bz;  // Controlled_Buffer controlled_buffer_1
  xor xor_1 (xor_1_out, Su, From_B_Register[7]);
  assign Output_To_Bus[6] = Eu ? full_adder_2_s : 1'bz;  // Controlled_Buffer controlled_buffer_2
  xor xor_2 (xor_2_out, Su, From_B_Register[6]);
  Full_Adder full_adder_2 (
    .A(From_Accumulator[6]), .B(xor_2_out), .Cin(full_adder_3_cout), .S(full_adder_2_s),
    .Cout(full_adder_2_cout));
  xor xor_3 (xor_3_out, Su, From_B_Register[5]);
  Full_Adder full_adder_3 (
    .A(From_Accumulator[5]), .B(xor_3_out), .Cin(full_adder_4_cout), .S(full_adder_3_s),
    .Cout(full_adder_3_cout));
  assign Output_To_Bus[5] = Eu ? full_adder_3_s : 1'bz;  // Controlled_Buffer controlled_buffer_3
  assign Output_To_Bus[4] = Eu ? full_adder_4_s : 1'bz;  // Controlled_Buffer controlled_buffer_4
  xor xor_4 (xor_4_out, Su, From_B_Register[4]);
  Full_Adder full_adder_4 (
    .A(From_Accumulator[4]), .B(xor_4_out), .Cin(full_adder_5_cout), .S(full_adder_4_s),
    .Cout(full_adder_4_cout));
  Full_Adder full_adder_5 (
    .A(From_Accumulator[3]), .B(xor_5_out), .Cin(full_adder_6_cout), .S(full_adder_5_s),
    .Cout(full_adder_5_cout));
  assign Output_To_Bus[3] = Eu ? full_adder_5_s : 1'bz;  // Controlled_Buffer controlled_buffer_5
  xor xor_5 (xor_5_out, Su, From_B_Register[3]);
  xor xor_6 (xor_6_out, Su, From_B_Register[2]);
  Full_Adder full_adder_6 (
    .A(From_Accumulator[2]), .B(xor_6_out), .Cin(full_adder_7_cout), .S(full_adder_6_s),
    .Cout(full_adder_6_cout));
  assign Output_To_Bus[2] = Eu ? full_adder_6_s : 1'bz;  // Controlled_Buffer controlled_buffer_6
  xor xor_7 (xor_7_out, Su, From_B_Register[1]);
  Full_Adder full_adder_7 (
    .A(From_Accumulator[1]), .B(xor_7_out), .Cin(full_adder_8_cout), .S(full_adder_7_s),
    .Cout(full_adder_7_cout));
  assign Output_To_Bus[1] = Eu ? full_adder_7_s : 1'bz;  // Controlled_Buffer controlled_buffer_7
  xor xor_8 (xor_8_out, Su, From_B_Register[0]);
  Full_Adder full_adder_8 (
    .A(From_Accumulator[0]), .B(xor_8_out), .Cin(Su), .S(full_adder_8_s), .Cout(full_adder_8_cout));
  assign Output_To_Bus[0] = Eu ? full_adder_8_s : 1'bz;  // Controlled_Buffer controlled_buffer_8

  // Notes on the sheet:
  //   Adder/Subtractor
endmodule

// Output
module Output_Register (
  input  [7:0] Input_From_Bus,
  input  Lo,
  input  CLK,
  input  CLR,
  input  Enable,
  output [7:0] Output_To_Binary_Display
);

  wire and_1_out, and_2_out, and_3_out, and_4_out, and_5_out, and_6_out, and_7_out, and_8_out, and_9_out,
       and_10_out, and_11_out, and_12_out, and_13_out, and_14_out, and_15_out, and_16_out, not_1_out,
       or_1_out, or_2_out, or_3_out, or_4_out, or_5_out, or_6_out, or_7_out, or_8_out;

  and and_1 (and_1_out, Output_To_Binary_Display[7], not_1_out);
  or or_1 (or_1_out, and_1_out, and_2_out);
  and and_2 (and_2_out, Input_From_Bus[7], Lo);
  D_Flip_Flop D7 (
    .clk(CLK), .D(or_1_out), .Q(Output_To_Binary_Display[7]), .en(Enable), .reset(CLR));  // open: Qn, preset
  and and_3 (and_3_out, Input_From_Bus[6], Lo);
  and and_4 (and_4_out, Output_To_Binary_Display[6], not_1_out);
  or or_2 (or_2_out, and_4_out, and_3_out);
  D_Flip_Flop D6 (
    .clk(CLK), .D(or_2_out), .Q(Output_To_Binary_Display[6]), .en(Enable), .reset(CLR));  // open: Qn, preset
  and and_5 (and_5_out, Output_To_Binary_Display[5], not_1_out);
  and and_6 (and_6_out, Input_From_Bus[5], Lo);
  or or_3 (or_3_out, and_5_out, and_6_out);
  and and_7 (and_7_out, Output_To_Binary_Display[4], not_1_out);
  D_Flip_Flop D5 (
    .clk(CLK), .D(or_3_out), .Q(Output_To_Binary_Display[5]), .en(Enable), .reset(CLR));  // open: Qn, preset
  and and_8 (and_8_out, Input_From_Bus[4], Lo);
  or or_4 (or_4_out, and_7_out, and_8_out);
  D_Flip_Flop D4 (
    .clk(CLK), .D(or_4_out), .Q(Output_To_Binary_Display[4]), .en(Enable), .reset(CLR));  // open: Qn, preset
  and and_9 (and_9_out, Output_To_Binary_Display[3], not_1_out);
  and and_10 (and_10_out, Input_From_Bus[3], Lo);
  or or_5 (or_5_out, and_9_out, and_10_out);
  D_Flip_Flop D3 (
    .clk(CLK), .D(or_5_out), .Q(Output_To_Binary_Display[3]), .en(Enable), .reset(CLR));  // open: Qn, preset
  and and_11 (and_11_out, Input_From_Bus[2], Lo);
  and and_12 (and_12_out, Output_To_Binary_Display[2], not_1_out);
  or or_6 (or_6_out, and_12_out, and_11_out);
  and and_13 (and_13_out, Output_To_Binary_Display[1], not_1_out);
  D_Flip_Flop D2 (
    .clk(CLK), .D(or_6_out), .Q(Output_To_Binary_Display[2]), .en(Enable), .reset(CLR));  // open: Qn, preset
  and and_14 (and_14_out, Input_From_Bus[1], Lo);
  or or_7 (or_7_out, and_13_out, and_14_out);
  D_Flip_Flop D1 (
    .clk(CLK), .D(or_7_out), .Q(Output_To_Binary_Display[1]), .en(Enable), .reset(CLR));  // open: Qn, preset
  and and_15 (and_15_out, Output_To_Binary_Display[0], not_1_out);
  or or_8 (or_8_out, and_15_out, and_16_out);
  not not_1 (not_1_out, Lo);
  and and_16 (and_16_out, Input_From_Bus[0], Lo);
  D_Flip_Flop D0 (
    .clk(CLK), .D(or_8_out), .Q(Output_To_Binary_Display[0]), .en(Enable), .reset(CLR));  // open: Qn, preset

  // Notes on the sheet:
  //   Fig- Output Register
endmodule

// RC
module RING_COUNTER (
  input  CLK,
  output T1,
  output T2,
  output T3,
  output T4,
  output T5,
  output T6
);

  wire not_1_out, or_1_out, or_2_out, or_3_out;

  not not_1 (not_1_out, or_1_out);
  or or_1 (or_1_out, or_2_out, or_3_out);
  or or_2 (or_2_out, T1, T2, T3);
  or or_3 (or_3_out, T4, T5, T6);
  D_Flip_Flop d_ff_1 (.clk(CLK), .D(not_1_out), .Q(T1));  // open: Qn, preset, en, reset
  D_Flip_Flop d_ff_2 (.clk(CLK), .D(T1), .Q(T2));  // open: Qn, preset, en, reset
  D_Flip_Flop d_ff_3 (.clk(CLK), .D(T2), .Q(T3));  // open: Qn, preset, en, reset
  D_Flip_Flop d_ff_4 (.clk(CLK), .D(T3), .Q(T4));  // open: Qn, preset, en, reset
  D_Flip_Flop d_ff_5 (.clk(CLK), .D(T4), .Q(T5));  // open: Qn, preset, en, reset
  D_Flip_Flop d_ff_6 (.clk(CLK), .D(T5), .Q(T6));  // open: Qn, preset, en, reset

  // Notes on the sheet:
  //   Fig: Ring Counter
endmodule
